# Fritzing sketch RFID without potentiometer (saved by Fritzing 0.8.7b)
breadboards: 1

parts:
  Part6 = Arduino Uno (Rev3) - ICSP
  LED3 = Green LED - Rect 5x2x7mm [package="5x2x7 mm [THT]"]
  LED4 = Red LED - Rect 5x2x7mm [package="5x2x7 mm [THT]"]
  Part7 = Adafruit DS1307 RTC Breakout [part_number="Adafruit #264"]
  R7 = Resistor [tolerance=±5% resistance=220 package=THT]
  LCD2 = LCD screen
  R9 = Resistor [tolerance=±5% resistance=220 package=THT]
  SD_card_module2 = SD Card Module
  Part8 = RFID-RC522-v2
  R10 = Resistor [tolerance=±5% resistance=220 package=THT]
  J1 = Piezo Speaker

nets:
  N1: Part6.A0, LCD2.DB4
  N2: Part6.A1, LCD2.DB5
  N3: Part6.A2, LCD2.DB6
  N4: Part6.A3, LCD2.DB7
  N5: Part6.A4/SDA, Part7.SDA
  N6: Part6.A5/SCL, Part7.SCL
  N7: Part6.ICSP_MISO, Part6.D12/MISO, Part8.MISO, R10.Pin_0
  N8: Part6.ICSP_MOSI, Part6.D11_PWM/MOSI, SD_card_module2.MOSI, Part8.MOSI
  N9: Part6.D9_PWM, Part8.RST
  N10: Part6.D10_PWM/SS, Part8.SDA
  N11: Part6.D13/SCK, SD_card_module2.SCK, Part8.SCK
  N12: Part6.D2, LCD2.E
  N13: Part6.D3_PWM, LCD2.RS
  N14: Part6.D4, SD_card_module2.CS
  N15: Part6.D5_PWM, J1.pin2
  N16: Part6.D6_PWM, R7.Pin_1
  N17: Part6.D7, R9.Pin_1
  N18: Part6.3V3, SD_card_module2.+3.3, Part8.3_3V
  5V: Part6.5V, Part7.VCC, LCD2.VDD, LCD2.LED+, SD_card_module2.+5
  GND: Part6.GND, LED3.cathode, LED4.cathode, Part7.GND, LCD2.VSS, LCD2.V0, LCD2.R/W, LCD2.LED-, SD_card_module2.GND, J1.pin1
  N19: SD_card_module2.MISO, R10.Pin_1

custom parts:
  Green LED - Rect 5x2x7mm: A generic rectangular green LED (~1.8V) 5mm x 2mm x 7mm
  Red LED - Rect 5x2x7mm: A generic rectangular red LED (~1.8V) 5mm x 2mm x 7mm
  Adafruit DS1307 RTC Breakout: This is a great battery-backed real time clock (RTC) that allows your microcontroller project to keep track of time even if it is reprogrammed, or if the power is lost. Perfect for datalogging, clock-building, time stamping, timers and alarms, etc. The DS1307 is the most popular RTC - but it requires 5V power to work (although we've used it with 5V power and 3.3V logic successfully) PCB &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
  SD Card Module: SD Card Module Slot Socket Reader For Arduino ARM MCU
  RFID-RC522-v2: A simple China made RFID-RC522 Reader; do check the pin labels, as this is a MFRC522 based clone.
