# Fritzing sketch RFID (saved by Fritzing 0.8.7b)

parts:
  R1 = Resistor [tolerance=±5% resistance=220 package=THT]
  R2 = Resistor [tolerance=±5% resistance=220 package=THT]
  R4 = Trimmer Potentiometer [maximum_resistance=10kΩ package=THT]
  Part3 = RFID-RC522-v2
  Part4 = Arduino Uno (Rev3) - ICSP
  LCD1 = LCD screen
  J1 = Piezo Speaker
  R5 = Resistor [tolerance=±5% resistance=220 package=THT]
  LED1 = Green LED - Rect 5x2x7mm [package="5x2x7 mm [THT]"]
  LED2 = Red LED - Rect 5x2x7mm [package="5x2x7 mm [THT]"]  # not connected
  Part5 = Adafruit DS1307 RTC Breakout [part_number="Adafruit #264"]  # not connected
  SD_card_module1 = SD Card Module

nets:
  N1: R1.Pin_0, Part3.MISO
  N2: R1.Pin_1, SD_card_module1.MISO
  N3: R2.Pin_1, Part4.D6_PWM
  N4: R4.leg1, LCD1.VDD
  N5: R4.wiper, LCD1.V0
  GND: R4.leg2, Part4.GND, LCD1.VSS, LED1.cathode
  N6: Part3.SDA, Part4.D10_PWM/SS
  N7: Part3.SCK, SD_card_module1.SCK
  N8: Part3.MOSI, SD_card_module1.MOSI
  N9: Part3.RST, Part4.D9_PWM
  N10: Part3.3_3V, Part4.3V3
  N11: Part4.A0, LCD1.DB4
  N12: Part4.A1, LCD1.DB5
  N13: Part4.A2, LCD1.DB6
  N14: Part4.A3, LCD1.DB7
  N15: Part4.D2, LCD1.E
  N16: Part4.D3_PWM, LCD1.RS
  N17: Part4.D4, SD_card_module1.CS
  N18: Part4.D5_PWM, J1.pin2
  N19: Part4.D7, R5.Pin_1

custom parts:
  RFID-RC522-v2: A simple China made RFID-RC522 Reader; do check the pin labels, as this is a MFRC522 based clone.
  Green LED - Rect 5x2x7mm: A generic rectangular green LED (~1.8V) 5mm x 2mm x 7mm
  Red LED - Rect 5x2x7mm: A generic rectangular red LED (~1.8V) 5mm x 2mm x 7mm
  Adafruit DS1307 RTC Breakout: This is a great battery-backed real time clock (RTC) that allows your microcontroller project to keep track of time even if it is reprogrammed, or if the power is lost. Perfect for datalogging, clock-building, time stamping, timers and alarms, etc. The DS1307 is the most popular RTC - but it requires 5V power to work (although we've used it with 5V power and 3.3V logic successfully) PCB &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
  SD Card Module: SD Card Module Slot Socket Reader For Arduino ARM MCU
